# Fritzing sketch 01-led-anschliessen (saved by Fritzing 0.9.3b)
breadboards: 1

parts:
  LED1 = smd LED [color="Green (555nm)" package="0805 [SMD]"]
  R3 = Resistor [tolerance=±5% resistance=220 package=THT]
  A1 = Espressif ESP32-S3 Nano Development Board

nets:
  N1: LED1.cathode, A1.GND
  N2: LED1.anode, R3.Pin_0
  N3: R3.Pin_1, A1.5V
