# Fritzing sketch 02-led-steuern (saved by Fritzing 0.9.3b)
circuit board: 8.46667cm x 5.64444cm
breadboards: 1

parts:
  Bauteil1 = Arduino Nano (Rev3.0)
  LED1 = smd LED [color="Green (555nm)" package="0805 [SMD]"]
  R1 = Resistor [tolerance=±5% resistance=220 package=THT]

nets (from the pcb view):
  N1: Bauteil1.GND, LED1.cathode
  N2: Bauteil1.5V, R1.Pin_0
  N3: LED1.anode, R1.Pin_1
