# Fritzing sketch 04-schalter-einlesen (saved by Fritzing 0.9.3b)
breadboards: 1

parts:
  S1 = Pushbutton [package="[THT]"]
  A1 = Espressif ESP32-S3 Nano Development Board

nets:
  N1: S1.Pin_1, S1.Pin_2
  N2: S1.Pin_3, S1.Pin_4, A1.02
