# Fritzing sketch 05-led-ueber-schalter-ansteuern (saved by Fritzing 0.9.3b)
circuit board: 8.46667cm x 5.64444cm
breadboards: 1

parts:
  Bauteil1 = Arduino Nano (Rev3.0)
  S1 = Pushbutton [package="[THT]"]
  LED2 = smd LED [color="Green (555nm)" package="0805 [SMD]"]
  R4 = Resistor [tolerance=±5% resistance=220 package=THT]

nets:
  N1: Bauteil1.GND, S1.Pin_1, S1.Pin_2, LED2.cathode
  N2: Bauteil1.D2, S1.Pin_3, S1.Pin_4
  N3: Bauteil1.D3, R4.Pin_1
  N4: LED2.anode, R4.Pin_0
