# Fritzing sketch 07-servo-ansteuern (saved by Fritzing 0.9.3b)
circuit board: 8.46667cm x 5.64444cm
breadboards: 1

parts:
  Bauteil1 = Arduino Nano (Rev3.0)
  J1 = Basic Servo
  S2 = H-Bridge with L298N
  VCC2 = Battery block 9V

nets:
  GND: Bauteil1.GND, J1.gnd, S2.GND, VCC2.-
  N1: Bauteil1.D5, J1.pulse
  VCC: J1.vcc, S2.5V
  N2: S2.12V, VCC2.+

custom parts:
  H-Bridge with L298N: h-bridge
