# Fritzing sketch 08-lichtsensor-benutzen (saved by Fritzing 0.9.3b)
circuit board: 8.46667cm x 5.64444cm
breadboards: 1

parts:
  R1 = PHOTOCELL [package=photocell]
  R2 = Resistor [tolerance=±5% resistance=1k package="0805 [SMD]"]
  µC = Arduino Nano (Rev3.0)

nets (from the pcb view):
  N1: R1.P$1, µC.5V
  N2: R2.Pin_0, µC.GND
  N3: R2.Pin_1, µC.A0
