# Fritzing sketch 09-lichtsensor-steuert-led (saved by Fritzing 0.9.3b)
breadboards: 1

parts:
  R2 = Resistor [tolerance=±5% resistance=1k package="0805 [SMD]"]
  R1 = PHOTOCELL [package=photocell]
  R4 = Resistor [tolerance=±5% resistance=220 package=THT]
  LED2 = smd LED [color="White (6500K)" package="0805 [SMD]"]
  A1 = Espressif ESP32-S3 Nano Development Board

nets:
  N1: R2.Pin_0, LED2.cathode, A1.GND
  N2: R2.Pin_1, R1.P$1, A1.01
  N3: R4.Pin_0, LED2.anode
  N4: R4.Pin_1, A1.02
