# Fritzing sketch 10-abstand-einlesen (saved by Fritzing 0.9.3b)
circuit board: 8.46667cm x 5.64444cm
breadboards: 1

parts:
  Bauteil1 = Arduino Nano (Rev3.0)
  hc-sr1 = hc-sr04
  S3 = H-Bridge with L298N
  VCC3 = Battery block 9V
  A2 = Espressif ESP32-S3 Nano Development Board  # not connected

nets:
  GND: Bauteil1.GND, hc-sr1.GND, S3.GND, VCC3.-
  N1: Bauteil1.D9, hc-sr1.Trig
  N2: Bauteil1.D10, hc-sr1.Echo
  VCC: hc-sr1.VCC, S3.5V
  N3: S3.12V, VCC3.+

custom parts:
  H-Bridge with L298N: h-bridge
