# Fritzing sketch line_follower (saved by Fritzing 0.9.3b)
circuit board: 8.46667cm x 5.64444cm
breadboards: 2

parts:
  Bauteil1 = Arduino Nano (Rev3.0)
  M2 = DC Motor
  S2 = H-Bridge with L298N
  VCC2 = Battery block 9V
  R2 = Resistor [tolerance=±5% resistance=220 package=THT]
  LED2 = smd LED [color="White (4500K)" package="0805 [SMD]"]
  R3 = Resistor [tolerance=±5% resistance=1k package="0805 [SMD]"]
  R4 = PHOTOCELL [package=photocell]
  M3 = DC Motor
  R5 = Resistor [tolerance=±5% resistance=1k package="0805 [SMD]"]
  R6 = Resistor [tolerance=±5% resistance=220 package=THT]
  LED3 = smd LED [color="White (4500K)" package="0805 [SMD]"]
  R7 = PHOTOCELL [package=photocell]

nets:
  GND: Bauteil1.GND, S2.GND, VCC2.-, LED2.cathode, R4.P$1, LED3.cathode, R7.P$1
  N1: Bauteil1.D5, S2.IN3
  N2: Bauteil1.D6, S2.IN2
  5V: Bauteil1.5V, S2.5V, S2.ENA, S2.ENB, R2.Pin_0, R3.Pin_1, R5.Pin_1, R6.Pin_0
  N3: Bauteil1.A1, R4.P$2, R5.Pin_0
  N4: Bauteil1.A0, R3.Pin_0, R7.P$2
  N5: M2.pin_1, S2.M2-02
  N6: M2.pin_2, S2.M2-01
  N7: S2.12V, VCC2.+
  N8: S2.M1-01, M3.pin_2
  N9: S2.M1-02, M3.pin_1
  N10: R2.Pin_1, LED3.anode
  N11: LED2.anode, R6.Pin_1

custom parts:
  H-Bridge with L298N: h-bridge
